// Logisim project ram-exemple.circ as structural Verilog: 1 circuit, main circuit main
module main (
  input  [12:0] in_1,
  output [7:0] out_2,
  output [7:0] out_3
);

  wire and_1_out, and_2_out, and_3_out, and_4_out, and_5_out, and_6_out, and_7_out, and_8_out, clock_1_out,
       decoder_1_out0, decoder_1_out1, decoder_2_out0, decoder_2_out1, decoder_2_out2, decoder_2_out3;
  wire [7:0] random_1_out, undriven;

  Decoder decoder_1 (.out0(decoder_1_out0), .out1(decoder_1_out1), .sel(in_1[12]));  // open: en
  Random random_1 (.clk(clock_1_out), .out(random_1_out));  // open: next, clr
  Clock clock_1 (.out(clock_1_out));
  Decoder #(.select(2)) decoder_2 (
    .out0(decoder_2_out0), .out1(decoder_2_out1), .out2(decoder_2_out2), .out3(decoder_2_out3),
    .sel(in_1[1:0]));  // open: en
  and and_1 (and_1_out, decoder_2_out0, decoder_1_out0);
  and and_2 (and_2_out, decoder_2_out1, decoder_1_out0);
  and and_3 (and_3_out, decoder_2_out2, decoder_1_out0);
  and and_4 (and_4_out, decoder_2_out3, decoder_1_out0);
  RAM #(.addrWidth(10), .bus("separate")) ram_1 (
    .addr(in_1[11:2]), .din(random_1_out), .data(out_2), .sel(and_1_out), .clk(clock_1_out));  // open: str, ld, clr
  RAM #(.addrWidth(10), .bus("separate")) ram_2 (
    .addr(in_1[11:2]), .din(random_1_out), .data(out_3), .sel(and_2_out), .clk(clock_1_out));  // open: str, ld, clr
  RAM #(.addrWidth(10), .bus("separate")) ram_3 (
    .addr(in_1[11:2]), .din(random_1_out), .sel(and_3_out), .clk(clock_1_out));  // open: data, str, ld, clr
  RAM #(.addrWidth(10), .bus("separate")) ram_4 (
    .addr(in_1[11:2]), .din(random_1_out), .sel(and_4_out), .clk(clock_1_out));  // open: data, str, ld, clr
  and and_5 (and_5_out, decoder_2_out0, decoder_1_out1);
  and and_6 (and_6_out, decoder_2_out1, decoder_1_out1);
  and and_7 (and_7_out, decoder_2_out2, decoder_1_out1);
  and and_8 (and_8_out, decoder_2_out3, decoder_1_out1);
  RAM #(.addrWidth(10), .bus("separate")) ram_5 (
    .addr(in_1[11:2]), .din(random_1_out), .sel(and_5_out), .clk(clock_1_out));  // open: data, str, ld, clr
  RAM #(.addrWidth(10), .bus("separate")) ram_6 (
    .addr(in_1[11:2]), .din(random_1_out), .sel(and_6_out), .clk(clock_1_out));  // open: data, str, ld, clr
  RAM #(.addrWidth(10), .bus("separate")) ram_7 (
    .addr(in_1[11:2]), .din(random_1_out), .sel(and_7_out), .clk(clock_1_out));  // open: data, str, ld, clr
  RAM #(.addrWidth(10), .bus("separate")) ram_8 (
    .addr(in_1[11:2]), .din(undriven), .sel(and_8_out), .clk(clock_1_out));  // open: data, str, ld, clr
  DotMatrix #(.matrixrows(8)) dotmatrix_1 (.col0(out_2));  // open: col1, col2, col3, col4
  DotMatrix #(.matrixrows(8)) dotmatrix_2 (.col0(out_3));  // open: col1, col2, col3, col4
endmodule
